# Fritzing sketch carrera_serial_without_esp (saved by Fritzing 0.9.4)
circuit board: 10cm x 8cm
breadboards: 1

parts:
  Level_Converter = I2C level shifter bidirectional
  J2 = Terminal Block - 2 pins [package=THT]
  J3 = Terminal Block - 2 pins [package=THT]
  J1 = Terminal Block - 2 pins [package=THT]
  RED = LED - 3mm [color="Red (633nm)" package="3 mm [THT]"]
  YELL = LED - 3mm [color="Yellow (595nm)" package="3 mm [THT]"]
  BLUE = LED - 3mm [color="Blue (525nm)" package="3 mm [THT]"]
  GREEN = LED - 3mm [color="Green (570nm)" package="3 mm [THT]"]
  R1 = Resistor [tolerance=±5% resistance=220 package=THT]
  R2 = Resistor [tolerance=±5% resistance=220 package=THT]
  R3 = Resistor [tolerance=±5% resistance=220 package=THT]
  R4 = Resistor [tolerance=±5% resistance=220 package=THT]
  ESP = female pin header, 8 pins [form="♀ (female)"]
  ESP_2 = female pin header, 8 pins [form="♀ (female)"]
  Voltage_Regulator = female pin header, 3 pins [form="♀ (female)"]

nets:
  N1: Level_Converter.LV4, ESP.pin2
  N2: Level_Converter.LV3, ESP.pin3
  N3: Level_Converter.GND, J2.Line_1, J3.Line_2, R1.Pin_1, R2.Pin_1, R3.Pin_1, R4.Pin_1, ESP_2.pin2, Voltage_Regulator.pin2
  N4: Level_Converter.LV, GREEN.anode, ESP.pin1
  N5: Level_Converter.HV, J2.Line_2, ESP_2.pin1, Voltage_Regulator.pin3
  N6: Level_Converter.HV3, J1.Line_1
  N7: Level_Converter.HV4, J1.Line_2
  N8: J3.Line_1, Voltage_Regulator.pin1
  N9: RED.cathode, R1.Pin_0
  N10: RED.anode, ESP.pin4
  N11: YELL.cathode, R2.Pin_0
  N12: YELL.anode, ESP.pin5
  N13: BLUE.cathode, R3.Pin_0
  N14: BLUE.anode, ESP.pin6
  N15: GREEN.cathode, R4.Pin_0

custom parts:
  Terminal Block - 2 pins: Generic Screw Terminal 9.5mm
